# Fritzing sketch c1 (saved by Fritzing 0.9.3b)
breadboards: 1

parts:
  Raspberry_Pi_1 = Raspberry Pi 3 [part_number=RPI-3-V1.2]
  LED1 = LED - 5mm [color="Red (633nm)" package="5 mm [THT]"]
  R3 = Resistor [tolerance=±5% resistance=220 package=THT]

nets:
  N1: Raspberry_Pi_1.GPIO18, R3.Pin_1
  N2: Raspberry_Pi_1.GND, LED1.cathode
  N3: LED1.anode, R3.Pin_0

notes:
  Circuito 1

// code stored in the sketch: Untitled3.ino
import RPi.GPIO as GPIO
import time
GPIO.setmode(GPIO.BOARD)
pin_to_circuit = 12
try:
    GPIO.setup(pin_to_circuit, GPIO.OUT)
    while(1):
        GPIO.output(pin_to_circuit,1)
        print("***LIGADO**")
        time.sleep(1)
        GPIO.output(pin_to_circuit,0)
        print("---DESLIGADO---")
        time.sleep(1)
except KeyboardInterrupt:
    print ("Fim")
    pass
finally:
    GPIO.cleanup()
